# Fritzing sketch wiring (saved by Fritzing 0.9.3b)
breadboards: 1

parts:
  Composant1 = Arduino Nano (Rev3.0)
  R1 = PHOTOCELL [package=photocell]
  J1 = Power Jack [package=power_jack_combo]
  MOTOR1 = Adafruit Gear-Reduced Stepper Motor (small)
  Composant2 = Adafruit DS3231 [part_number="Adafruit #3013"]
  Composant4 = Adafruit MAX4466 Electret Microphone Amplifier [part_number="Adafruit #1063"]
  ULN2003A_-_Stepper_Driver_Board1 = ULN2003A - Stepper Driver Board [package=board]
  S1 = Taiway 100-SP-X-T1 SPDT Miniature Toggle Switch [part_number=100-SP-X-T1-0-0-B1-M1 package=THT]  # not connected
  S2 = Taiway 100-SP-X-T1 SPDT Miniature Toggle Switch [part_number=100-SP-X-T1-0-0-B1-M1 package=THT]  # not connected
  S3 = Momentary Switch [package=tactile-pth]  # not connected
  Composant6 = Adafruit Bluefruit LE UART Friend [part_number="Adafruit #2479"]
  R2 = Resistor [tolerance=±5% resistance=10k package="2010 [SMD]"]

nets:
  GND: Composant1.GND, J1.GNDBREAK, Composant2.GND, Composant4.GND, ULN2003A_-_Stepper_Driver_Board1.GND, Composant6.GND, R2.Pin_0
  N1: Composant1.D2, Composant2.SDA
  N2: Composant1.D3, Composant2.SCL
  N3: Composant1.D5, Composant6.RTS
  N4: Composant1.D6, Composant6.RXI
  N5: Composant1.D7, Composant6.TXO
  N6: Composant1.D8, Composant6.CTS
  N7: Composant1.D9, ULN2003A_-_Stepper_Driver_Board1.IN4
  N8: Composant1.D10, ULN2003A_-_Stepper_Driver_Board1.IN3
  N9: Composant1.D11/MOSI, ULN2003A_-_Stepper_Driver_Board1.IN2
  N10: Composant1.D12/MISO, ULN2003A_-_Stepper_Driver_Board1.IN1
  VIN: Composant1.VIN, J1.PWR, ULN2003A_-_Stepper_Driver_Board1.VCC
  VIN_2: Composant1.5V, R1.P$2, Composant2.Vin, Composant4.VCC, Composant6.VIN
  N11: Composant1.A1, Composant4.OUT
  N12: Composant1.A0, R1.P$1, R2.Pin_1
  N13: MOTOR1.RED, ULN2003A_-_Stepper_Driver_Board1.C
  N14: MOTOR1.ORANGE, ULN2003A_-_Stepper_Driver_Board1.D
  N15: MOTOR1.YELLOW, ULN2003A_-_Stepper_Driver_Board1.E
  N16: MOTOR1.PINK, ULN2003A_-_Stepper_Driver_Board1.F
  N17: MOTOR1.BLUE, ULN2003A_-_Stepper_Driver_Board1.G

custom parts:
  Adafruit Gear-Reduced Stepper Motor (small): Adafruit gear-reduction stepper motor (small)
  Adafruit DS3231: The datasheet for the DS3231 explains that this part is an "Extremely Accurate I²C-Integrated RTC/TCXO/Crystal". And, hey, it does exactly what it says on the tin! This Real Time Clock (RTC) is the most precise you can get in a small, low power package. Most RTCs use an external 32kHz timing crystal that is used to keep time with low current draw. And that's all well and good, but those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
  Adafruit MAX4466 Electret Microphone Amplifier: Add an ear to your project with this well-designed electret microphone amplifier. This fully assembled and tested board comes with a 20-20KHz electret microphone soldered on. For the amplification, we use the Maxim MAX4466, an op-amp specifically designed for this delicate task! The amplifier has excellent power supply noise rejection, so this amplifier sounds really good and isn't nearly as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
  ULN2003A - Stepper Driver Board: A common stepper motor driver board based on ULN2003APG darlington array
  Adafruit Bluefruit LE UART Friend: The Bluefruit LE UART Friend makes it easy to add Bluetooth Low Energy connectivity to anything with a hardware or software serial port. We even have nice hardware flow control so you won't have to think about losing data. Connect to your Arduino or other microcontroller or even just a standard FTDI cable for debugging and testing.
